// Logisim project PROJVv1.circ as structural Verilog: 4 circuits, main circuit 4-bit compititor
module _4_bit_compititor (
  input  A3,
  input  B3,
  input  A2,
  input  B2,
  input  A1,
  input  B1,
  input  A0,
  input  B0,
  output out_9,
  output out_10,
  output out_11,
  output out_12,
  output out_13,
  output out_14,
  output out_15,
  output out_16,
  output out_17,
  output out_18,
  output out_19,
  output out_20,
  output out_21,
  output out_22,
  output out_23,
  output out_24,
  output out_25
);

  wire and_1_out, and_2_out, and_3_out, and_4_out, and_5_out, and_6_out, and_7_out, and_8_out, and_9_out,
       and_10_out, and_11_out, and_12_out, and_13_out, and_14_out, nor_1_out, nor_2_out, nor_3_out,
       nor_4_out, not_1_out, not_2_out, not_3_out, not_4_out, not_5_out, not_6_out, not_7_out, not_8_out;

  not not_1 (not_1_out, B3);
  not not_2 (not_2_out, A3);
  not not_3 (not_3_out, B2);
  not not_4 (not_4_out, A2);
  not not_5 (not_5_out, B1);
  not not_6 (not_6_out, A1);
  not not_7 (not_7_out, B0);
  not not_8 (not_8_out, A0);
  and and_1 (and_1_out, A2, not_3_out);
  and and_2 (and_2_out, not_4_out, B2);
  and and_3 (and_3_out, A1, not_5_out);
  and and_4 (and_4_out, not_6_out, B1);
  and and_5 (and_5_out, A0, not_7_out);
  and and_6 (and_6_out, not_8_out, B0);
  and and_7 (and_7_out, A3, not_1_out);
  and and_8 (and_8_out, not_2_out, B3);
  nor nor_1 (nor_1_out, and_7_out, and_8_out);
  nor nor_2 (nor_2_out, and_1_out, and_2_out);
  nor nor_3 (nor_3_out, and_3_out, and_4_out);
  nor nor_4 (nor_4_out, and_5_out, and_6_out);
  and and_9 (and_9_out, nor_1_out, and_1_out);
  and and_10 (and_10_out, nor_1_out, and_2_out);
  and and_11 (and_11_out, nor_1_out, nor_2_out, and_4_out);
  and and_12 (and_12_out, nor_3_out, nor_2_out, nor_1_out, and_6_out);
  and and_13 (and_13_out, nor_2_out, nor_1_out, and_3_out);
  and and_14 (and_14_out, nor_3_out, nor_2_out, nor_1_out, and_5_out);
  or or_1 (out_23, and_7_out, and_9_out, and_13_out, and_14_out);
  or or_2 (out_24, and_8_out, and_10_out, and_11_out, and_12_out);
  and and_15 (out_25, nor_1_out, nor_2_out, nor_3_out, nor_4_out);
  binnary_to_hex binnary_to_hex_1 (
    .a3(B3), .a2(B2), .a1(B1), .a0(B0), .a(out_9), .b(out_10), .c(out_11), .d(out_12), .e(out_13),
    .f(out_14), .g(out_15));
  binnary_to_hex binnary_to_hex_2 (
    .a3(A3), .a2(A2), .a1(A1), .a0(A0), .a(out_16), .b(out_17), .c(out_18), .d(out_19), .e(out_20),
    .f(out_21), .g(out_22));

  // Notes on the sheet:
  //   A3.B3'
  //   A3'.B3
  //   A2.B2'
  //   A2'.B2
  //   A1.B1'
  //   A1'.B1
  //   A0.B0'
  //   A0'.B0
  //   X3
  //   X2
  //   X1
  //   X0
  //   A2.B2'.X3
  //   A2'.B2.X3
  //   A1.B1'.X3.X2
  //   A1'.B1.X2.X3
  //   A0.B0'.X1.X2.X3
  //   A0'.B0.X1.X2.X3
  //   A>B
  //   A<B
  //   A=B
endmodule

module BSE_decoder (
  input  Bg,
  input  Sl,
  input  Eq,
  output a,
  output b,
  output c,
  output d,
  output e,
  output f,
  output g
);

  wire and_2_out, and_3_out, and_4_out, and_6_out, and_7_out, and_8_out, not_1_out, not_2_out, not_3_out,
       not_4_out, not_5_out, not_6_out, not_7_out, not_8_out, not_9_out, not_10_out, not_11_out, not_12_out,
       not_13_out, not_14_out, not_15_out, not_16_out;

  not not_1 (not_1_out, Sl);
  not not_2 (not_2_out, Eq);
  not not_3 (not_3_out, Bg);
  not not_4 (not_4_out, Sl);
  not not_5 (not_5_out, Bg);
  not not_6 (not_6_out, Eq);
  not not_7 (not_7_out, Sl);
  not not_8 (not_8_out, Eq);
  not not_9 (not_9_out, Bg);
  not not_10 (not_10_out, Eq);
  not not_11 (not_11_out, Bg);
  not not_12 (not_12_out, Sl);
  not not_13 (not_13_out, Bg);
  not not_14 (not_14_out, Eq);
  not not_15 (not_15_out, Sl);
  not not_16 (not_16_out, Eq);
  and and_1 (c, Bg, not_1_out, not_2_out);
  and and_2 (and_2_out, not_3_out, not_4_out, Eq);
  and and_3 (and_3_out, not_5_out, Sl, not_6_out);
  and and_4 (and_4_out, Bg, not_7_out, not_8_out);
  and and_5 (e, not_9_out, Sl, not_10_out);
  and and_6 (and_6_out, not_11_out, not_12_out, Eq);
  and and_7 (and_7_out, not_13_out, Sl, not_14_out);
  and and_8 (and_8_out, Bg, not_15_out, not_16_out);
  or or_1 (d, and_2_out, and_3_out, and_4_out);
  or or_2 (g, and_6_out, and_7_out, and_8_out);

  assign a = 1'b0;
  assign b = 1'b0;
  assign f = 1'b0;
endmodule

module Main_circuit (
  input  A3,
  input  A2,
  input  A1,
  input  A0,
  input  B3,
  input  B2,
  input  B1,
  input  B0
);

  wire a1_t, a2_t, b1_t, b2_t, b2da, b2db, b2dc, b2dd, b2de, b2df, b2dg, bigger, c1, c2, d1, d2, e1, e2,
       equal, f1, f2, g1, g2, smaller;

  _4_bit_compititor u_4_bit_compititor_1 (
    .A3(A3), .B3(B3), .A2(A2), .B2(B2), .A1(A1), .B1(B1), .A0(A0), .B0(B0), .out_9(a1_t), .out_10(b1_t),
    .out_11(c1), .out_12(d1), .out_13(e1), .out_14(f1), .out_15(g1), .out_16(a2_t), .out_17(b2_t),
    .out_18(c2), .out_19(d2), .out_20(e2), .out_21(f2), .out_22(g2), .out_23(bigger), .out_24(smaller),
    .out_25(equal));
  _7_Segment_Display u_7_segment_display_1 (.g(g2), .f(f2), .a(a2_t), .b(b2_t), .e(e2), .d(d2), .c(c2));  // open: dp
  BSE_decoder bse_decoder_1 (
    .Bg(bigger), .Sl(smaller), .Eq(equal), .a(b2da), .b(b2db), .c(b2dc), .d(b2dd), .e(b2de), .f(b2df),
    .g(b2dg));
  _7_Segment_Display u_7_segment_display_2 (
    .g(b2dg), .f(b2df), .a(b2da), .b(b2db), .e(b2de), .d(b2dd), .c(b2dc));  // open: dp
  _7_Segment_Display u_7_segment_display_3 (.g(g1), .f(f1), .a(a1_t), .b(b1_t), .e(e1), .d(d1), .c(c1));  // open: dp
endmodule

module binnary_to_hex (
  input  a3,
  input  a2,
  input  a1,
  input  a0,
  output a,
  output b,
  output c,
  output d,
  output e,
  output f,
  output g
);

  wire and_1_out, and_2_out, and_3_out, and_4_out, and_5_out, and_6_out, and_7_out, and_8_out, and_9_out,
       and_10_out, and_11_out, and_12_out, and_13_out, and_14_out, and_15_out, and_16_out, and_17_out,
       and_18_out, and_19_out, and_20_out, and_21_out, and_22_out, and_23_out, and_24_out, and_25_out,
       and_26_out, and_27_out, and_28_out, and_29_out, and_30_out, and_31_out, and_32_out, and_33_out,
       and_34_out, and_35_out, and_36_out, not_1_out, not_2_out, not_3_out, not_4_out, not_5_out, not_6_out,
       not_7_out, not_8_out, not_9_out, not_10_out, not_11_out, not_12_out, not_13_out, not_14_out,
       not_15_out, not_16_out, not_17_out, not_18_out, not_19_out, not_20_out, not_21_out, not_22_out,
       not_23_out, not_24_out, not_25_out, not_26_out, not_27_out, not_28_out, not_29_out, not_30_out,
       not_31_out, not_32_out, not_33_out, not_34_out, not_35_out, not_36_out, not_37_out, not_38_out,
       not_39_out, not_40_out, not_41_out, not_42_out, not_43_out, not_44_out, not_45_out;

  not not_1 (not_1_out, a2);
  and and_1 (and_1_out, not_1_out, not_2_out);
  not not_2 (not_2_out, a0);
  not not_3 (not_3_out, a3);
  and and_2 (and_2_out, not_3_out, a1);
  not not_4 (not_4_out, a3);
  and and_3 (and_3_out, not_4_out, a2, a0);
  and and_4 (and_4_out, a2, a1);
  and and_5 (and_5_out, a3, not_5_out, not_6_out);
  not not_5 (not_5_out, a2);
  not not_6 (not_6_out, a1);
  and and_6 (and_6_out, a3, not_7_out);
  not not_7 (not_7_out, a0);
  not not_8 (not_8_out, a3);
  and and_7 (and_7_out, not_8_out, not_9_out);
  not not_9 (not_9_out, a2);
  not not_10 (not_10_out, a3);
  not not_11 (not_11_out, a1);
  and and_8 (and_8_out, not_10_out, not_11_out, not_12_out);
  not not_12 (not_12_out, a0);
  not not_13 (not_13_out, a2);
  and and_9 (and_9_out, not_13_out, not_14_out);
  not not_14 (not_14_out, a1);
  not not_15 (not_15_out, a3);
  and and_10 (and_10_out, not_15_out, a1, a0);
  and and_11 (and_11_out, a3, not_16_out, a0);
  not not_16 (not_16_out, a1);
  and and_12 (and_12_out, a3, a1, not_17_out);
  not not_17 (not_17_out, a0);
  not not_18 (not_18_out, a3);
  and and_13 (and_13_out, not_18_out, not_19_out);
  not not_19 (not_19_out, a1);
  not not_20 (not_20_out, a3);
  and and_14 (and_14_out, not_20_out, a0);
  not not_21 (not_21_out, a1);
  and and_15 (and_15_out, not_21_out, a0);
  not not_22 (not_22_out, a3);
  and and_16 (and_16_out, not_22_out, a2);
  and and_17 (and_17_out, a3, not_23_out);
  not not_23 (not_23_out, a2);
  not not_24 (not_24_out, a3);
  and and_18 (and_18_out, not_24_out, not_25_out, not_26_out);
  not not_25 (not_25_out, a2);
  not not_26 (not_26_out, a0);
  not not_27 (not_27_out, a2);
  and and_19 (and_19_out, not_27_out, a1, a0);
  and and_20 (and_20_out, a2, not_28_out, a0);
  not not_28 (not_28_out, a1);
  and and_21 (and_21_out, a2, a1, not_29_out);
  not not_29 (not_29_out, a0);
  and and_22 (and_22_out, a3, not_30_out, not_31_out);
  not not_30 (not_30_out, a1);
  not not_31 (not_31_out, a0);
  not not_32 (not_32_out, a2);
  and and_23 (and_23_out, not_32_out, not_33_out);
  not not_33 (not_33_out, a0);
  and and_24 (and_24_out, a1, not_34_out);
  not not_34 (not_34_out, a0);
  and and_25 (and_25_out, a3, a1);
  and and_26 (and_26_out, a3, a2);
  not not_35 (not_35_out, a1);
  and and_27 (and_27_out, not_35_out, not_36_out);
  not not_36 (not_36_out, a0);
  not not_37 (not_37_out, a3);
  and and_28 (and_28_out, not_37_out, a2, not_38_out);
  not not_38 (not_38_out, a1);
  and and_29 (and_29_out, a2, not_39_out);
  not not_39 (not_39_out, a0);
  and and_30 (and_30_out, a3, not_40_out);
  not not_40 (not_40_out, a2);
  and and_31 (and_31_out, a3, a1);
  not not_41 (not_41_out, a2);
  and and_32 (and_32_out, not_41_out, a1);
  and and_33 (and_33_out, a1, not_42_out);
  not not_42 (not_42_out, a0);
  not not_43 (not_43_out, a3);
  and and_34 (and_34_out, not_43_out, a2, not_44_out);
  not not_44 (not_44_out, a1);
  and and_35 (and_35_out, a3, not_45_out);
  not not_45 (not_45_out, a2);
  and and_36 (and_36_out, a3, a0);
  or or_1 (c, and_13_out, and_14_out, and_15_out, and_16_out, and_17_out);
  or or_2 (d, and_18_out, and_19_out, and_20_out, and_21_out, and_22_out);
  or or_3 (e, and_23_out, and_24_out, and_25_out, and_26_out);
  or or_4 (f, and_27_out, and_28_out, and_29_out, and_30_out, and_31_out);
  or or_5 (g, and_32_out, and_33_out, and_34_out, and_35_out, and_36_out);
  or or_6 (a, and_1_out, and_2_out, and_3_out, and_4_out, and_5_out, and_6_out);
  or or_7 (b, and_7_out, and_8_out, and_9_out, and_10_out, and_11_out, and_12_out);
endmodule
